# Fritzing sketch Schematic (saved by Fritzing 0.9.3b)
breadboards: 1

parts:
  Part1 = Arduino Uno (Rev3) - ICSP
  J1 = Basic Servo
  J2 = Basic Servo
  J3 = Basic Servo
  PWM1 = PCA9685 16x12-bit PWM Breakout
  R1 = Resistor [tolerance=±5% resistance=220 package="2010 [SMD]"]
  R2 = Rotary Potentiometer (Large) [maximum_resistance=100kΩ package=THT]
  R3 = Rotary Potentiometer (Large) [maximum_resistance=100kΩ package=THT]
  R4 = Rotary Potentiometer (Large) [maximum_resistance=100kΩ package=THT]
  S1 = Pushbutton [package="[SMD]"]
  JACK1 = 2.1mm Barrel Jack with Terminal Block  # not connected

nets:
  N1: Part1.A0, R2.wiper
  N2: Part1.A1, R3.wiper
  N3: Part1.A2, R4.wiper
  N4: Part1.A4/SDA, PWM1.no_name_yet#504
  N5: Part1.A5/SCL, PWM1.no_name_yet#503
  N6: Part1.D2, R1.Pin_1, S1.Pin_3, S1.Pin_4
  N7: Part1.5V, PWM1.no_name_yet#505
  GND: Part1.GND, J1.gnd, J2.gnd, J3.gnd, PWM1.no_name_yet#501, PWM1.no_name_yet#1000, PWM1.no_name_yet#1001, PWM1.no_name_yet#1002
  VCC: J1.vcc, J2.vcc, J3.vcc, PWM1.no_name_yet#100, PWM1.no_name_yet#101, PWM1.no_name_yet#102
  N8: J1.pulse, PWM1.no_name_yet#2
  N9: J2.pulse, PWM1.no_name_yet#1
  N10: J3.pulse, PWM1.no_name_yet#0
  N11: R1.Pin_0, R4.leg2
  N12: R2.leg1, S1.Pin_1, S1.Pin_2
